# Fritzing sketch Arduino Clock(Fritzing Sketch) (saved by Fritzing 0.9.6b)
circuit board: 8.46667cm x 5.64444cm
breadboards: 1

parts:
  R4 = Resistor [package=THT]
  S1 = Pushbutton [package="[THT]"]
  R5 = Resistor [package=THT]
  R7 = Resistor [package=THT]
  LED1 = RGB LED (com. anode, rbg) [package="5 mm [THT]"]
  R6 = Resistor [package=THT]
  J2 = Piezo Speaker
  Componente1 = Arduino Uno (Rev3)
  R2 = Resistor [package=THT]
  S2 = Pushbutton [package="[THT]"]
  R3 = Resistor [package=THT]
  J3 = Basic Servo
  SM1 = 28BYJ-48 Stepper Motor [part_number=28BYJ-48]
  Driver1 = 28BYJ-48 Driver Module [part_number=ULN2003 package=THT]

nets (from the schematic view):
  N1: R4.Pin_1, Componente1.D12/MISO
  N2: S1.Pin_1, S1.Pin_2, Componente1.D2, R2.Pin_0
  N3: S1.Pin_3, S1.Pin_4, Componente1.5V
  N4: R5.Pin_1, Componente1.D13/SCK
  N5: R7.Pin_1, J2.pin2
  N6: LED1.common_anode, J3.vcc
  N7: LED1.green_cathode, R6.Pin_0
  N8: R6.Pin_1, Componente1.D5_PWM
  N9: Componente1.D8, Driver1.IN1
  N10: Componente1.D9_PWM, Driver1.IN2
  N11: Componente1.D10_PWM/SS, Driver1.IN3
  N12: Componente1.D11_PWM/MOSI, Driver1.IN4
  N13: Componente1.GND, R3.Pin_1
  N14: Componente1.D3_PWM, J3.pulse
  N15: Componente1.D4, S2.Pin_1, S2.Pin_2, R3.Pin_0
  N16: S2.Pin_3, S2.Pin_4
  N17: SM1.yellow-pin, Driver1.yellow-pin

custom parts:
  Resistor: A generic 5-band resistor (0.25W)
  28BYJ-48 Stepper Motor: Unipolar Stepper Motor 28BYJ-48 Top coil - pink & orange Bottom coil - blue & yellow Common rail - red Connector pins: blue - pink - yellow - orange - red
  28BYJ-48 Driver Module: ULN2003 Driver Module for the 28BYJ-48 Unipolar Stepper Motor LED A - Blue wire - Bottom coil left LED B - Pink wire - Top coil left LED C - Yellow wire - Bottom coil right LED D - Orange wire - Top coil right Common rail - red Connector pins: blue - pink - yellow - orange - red Control pins - IN1 to IN4 Power pins - GND & Vmotor (5-12V) On/Off jumper (if removed, power to motor is cut).

// code stored in the sketch: homework.ino
#include "MotorClock.h"
const int hours = 15;
const int minutes = 37;
const int servoP = 3;
const int stepperN1P = 8;
const int stepperN2P = 9;
const int stepperN3P = 10;
const int stepperN4P = 11;
const int buzzer = 6;
const int buttonI = 4;
const int buttonII = 2;
const int rgbRP = 12;
const int rgbGP = 13;
const int rgbBP = 5;

void setup(){
  MotorClock* MC  = new MotorClock(hours,minutes,servoP,stepperN1P,stepperN2P,stepperN3P,stepperN4P,buzzer,buttonI,buttonII,rgbRP,rgbGP,rgbBP);
  Serial.begin(9600);
  
}

void loop() {
 
}
